// Logisim project control-logic.circ as structural Verilog: 1 circuit, main circuit control_logic
module control_logic (
  input  [31:0] inst,
  input  BrEq,
  input  BrLt,
  output PCSel,
  output RegWEn,
  output [2:0] ImmSel,
  output BrUn,
  output ASel,
  output BSel,
  output [3:0] ALUSel,
  output MemRW,
  output [1:0] WBSel,
  output CSRSel,
  output CSRWen
);

  wire and_1_out, and_2_out, and_3_out, and_4_out, and_5_out, and_6_out, and_7_out, and_8_out, and_9_out,
       comparator_1_eq, comparator_2_eq, comparator_3_eq, comparator_4_eq, comparator_5_eq, comparator_6_eq,
       comparator_7_eq, comparator_8_eq, comparator_9_eq, comparator_10_eq, comparator_11_eq,
       comparator_12_eq, comparator_13_eq, comparator_14_eq, comparator_15_eq, comparator_16_eq,
       comparator_17_eq, comparator_18_eq, comparator_19_eq, comparator_19_gt, comparator_20_eq,
       comparator_21_eq, comparator_22_eq;
  wire [4:0] i, r;
  wire [5:0] iinst;

  Multiplexer #(.enable("false"), .width(6)) multiplexer_1 (
    .in0({1'b0, i}), .in1({1'b0, r}), .out(iinst), .sel(comparator_1_eq));
  Comparator #(.width(7)) comparator_1 (.a(7'b0110011), .b(inst[6:0]), .eq(comparator_1_eq));  // open: gt, lt
  Comparator #(.mode("unsigned"), .width(3)) comparator_2 (
    .a(3'b000), .b(inst[14:12]), .eq(comparator_2_eq));  // open: gt, lt
  Comparator #(.mode("unsigned"), .width(3)) comparator_3 (
    .a(3'b001), .b(inst[14:12]), .eq(comparator_3_eq));  // open: gt, lt
  Comparator #(.mode("unsigned"), .width(3)) comparator_4 (
    .a(3'b010), .b(inst[14:12]), .eq(comparator_4_eq));  // open: gt, lt
  Comparator #(.mode("unsigned"), .width(3)) comparator_5 (
    .a(3'b100), .b(inst[14:12]), .eq(comparator_5_eq));  // open: gt, lt
  Comparator #(.mode("unsigned"), .width(3)) comparator_6 (
    .a(3'b101), .b(inst[14:12]), .eq(comparator_6_eq));  // open: gt, lt
  Comparator #(.mode("unsigned"), .width(3)) comparator_7 (
    .a(3'b110), .b(inst[14:12]), .eq(comparator_7_eq));  // open: gt, lt
  Comparator #(.mode("unsigned"), .width(3)) comparator_8 (
    .a(3'b111), .b(inst[14:12]), .eq(comparator_8_eq));  // open: gt, lt
  Comparator #(.mode("unsigned"), .width(3)) comparator_9 (
    .a(3'b000), .b(inst[14:12]), .eq(comparator_9_eq));  // open: gt, lt
  Comparator #(.mode("unsigned"), .width(3)) comparator_10 (
    .a(3'b001), .b(inst[14:12]), .eq(comparator_10_eq));  // open: gt, lt
  Comparator #(.mode("unsigned"), .width(3)) comparator_11 (
    .a(3'b010), .b(inst[14:12]), .eq(comparator_11_eq));  // open: gt, lt
  Comparator #(.mode("unsigned"), .width(3)) comparator_12 (
    .a(3'b011), .b(inst[14:12]), .eq(comparator_12_eq));  // open: gt, lt
  Comparator #(.mode("unsigned"), .width(3)) comparator_13 (
    .a(3'b100), .b(inst[14:12]), .eq(comparator_13_eq));  // open: gt, lt
  Comparator #(.mode("unsigned"), .width(3)) comparator_14 (
    .a(3'b101), .b(inst[14:12]), .eq(comparator_14_eq));  // open: gt, lt
  Comparator #(.mode("unsigned"), .width(3)) comparator_15 (
    .a(3'b110), .b(inst[14:12]), .eq(comparator_15_eq));  // open: gt, lt
  Comparator #(.mode("unsigned"), .width(3)) comparator_16 (
    .a(3'b111), .b(inst[14:12]), .eq(comparator_16_eq));  // open: gt, lt
  Comparator #(.mode("unsigned"), .width(7)) comparator_17 (
    .a(7'b0110011), .b(inst[6:0]), .eq(comparator_17_eq));  // open: gt, lt
  Comparator #(.mode("unsigned"), .width(7)) comparator_18 (
    .a(7'b0010011), .b(inst[6:0]), .eq(comparator_18_eq));  // open: gt, lt
  Comparator #(.mode("unsigned"), .width(2)) comparator_19 (
    .a(inst[31:30]), .b(2'b00), .gt(comparator_19_gt), .eq(comparator_19_eq));  // open: lt
  Comparator #(.mode("unsigned"), .width(7)) comparator_20 (
    .a({7{1'b0}}), .b(inst[31:25]), .eq(comparator_20_eq));  // open: gt, lt
  Comparator #(.mode("unsigned"), .width(7)) comparator_21 (
    .a(7'b0000001), .b(inst[31:25]), .eq(comparator_21_eq));  // open: gt, lt
  Comparator #(.mode("unsigned"), .width(7)) comparator_22 (
    .a(7'b0100000), .b(inst[31:25]), .eq(comparator_22_eq));  // open: gt, lt
  ROM #(.addrWidth(6), .dataWidth(16)) rom_1 (
    .addr(iinst), .data({RegWEn, ImmSel, BrUn, ASel, BSel, ALUSel, MemRW, WBSel, CSRSel, CSRWen}));
  and and_1 (and_1_out, comparator_6_eq, comparator_19_eq);
  and and_2 (and_2_out, comparator_6_eq, comparator_19_gt);
  and and_3 (and_3_out, comparator_10_eq, comparator_20_eq);
  and and_4 (and_4_out, comparator_10_eq, comparator_21_eq);
  and and_5 (and_5_out, comparator_14_eq, comparator_20_eq);
  and and_6 (and_6_out, comparator_14_eq, comparator_22_eq);
  Priority_Encoder #(.select(5)) priority_encoder_1 (
    .in15(comparator_2_eq), .in16(comparator_3_eq), .in17(comparator_4_eq), .in18(comparator_5_eq),
    .in19(and_1_out), .in20(and_2_out), .in21(comparator_7_eq), .in22(comparator_8_eq), .out(i),
    .en_in(comparator_18_eq));  // open: in0, in1, in2, in3, in4, in5, in6, in7, in8, in9, in10, in11, in12, in13, in14, in23, in24, in25, in26, in27, in28, in29, in30, in31, gs, en_out
  and and_7 (and_7_out, comparator_9_eq, comparator_20_eq);
  and and_8 (and_8_out, comparator_9_eq, comparator_21_eq);
  and and_9 (and_9_out, comparator_9_eq, comparator_22_eq);
  Priority_Encoder #(.select(5)) priority_encoder_2 (
    .in0(and_7_out), .in1(and_8_out), .in2(and_9_out), .in3(and_3_out), .in4(and_4_out),
    .in5(comparator_12_eq), .in6(comparator_11_eq), .in7(comparator_13_eq), .in8(and_5_out), .in9(and_6_out),
    .in10(comparator_15_eq), .in11(comparator_16_eq), .out(r), .en_in(comparator_17_eq));  // open: in12, in13, in14, in15, in16, in17, in18, in19, in20, in21, in22, in23, in24, in25, in26, in27, in28, in29, in30, in31, gs, en_out

  assign PCSel = 1'b0;

  // Other names for the same wires on the sheet: opcode[6:0] = inst[6:0]

  // Notes on the sheet:
  //   INPUTS to your circuit
  //   contents of rom_1 (hex, n*v repeats v):
  //   9004 9104 9184 9024 9124 9164 9044 9084 90a4 91a4 90c4 90e4 0 0 9200 9204 9224 9244 9284 92a4 93a4
  //   92c4 92e4
  //   ROM FOR CONTROL LOGIC
  //   DON'T CHANGE THE LOCATIONS OF THE INPUTS AND OUTPUTS!
  //   OUTPUT from your circuit
  //   Reminder: Use combinational logic for PCSel
endmodule
